# Fritzing sketch Vitrine_Fan_Control (saved by Fritzing 0.9.9b)

parts:
  WeMos_D1_Mini1 = WeMos D1 Mini
  R2 = Resistor [tolerance=±1% power=0.25 resistance=2.2k package=THT]
  PWM_Fan_(+5V)_-_Noctua_NF-F12 = Fan - 4 wire [package=THT]
  Bauteil1 = Adafruit SHT31-D [part_number="Adafruit #2857"]

nets:
  N1: WeMos_D1_Mini1.3V3, R2.Pin_0
  N2: WeMos_D1_Mini1.5V, PWM_Fan_(+5V)_-_Noctua_NF-F12.Power
  N3: WeMos_D1_Mini1.D0, Bauteil1.SDA
  N4: WeMos_D1_Mini1.D1, PWM_Fan_(+5V)_-_Noctua_NF-F12.Tach
  N5: WeMos_D1_Mini1.D2, R2.Pin_1, PWM_Fan_(+5V)_-_Noctua_NF-F12.PWM
  N6: WeMos_D1_Mini1.D5, Bauteil1.SCL
  N7: WeMos_D1_Mini1.G, PWM_Fan_(+5V)_-_Noctua_NF-F12.GND

custom parts:
  Fan - 4 wire: Fan, 4 wire with tach.
  Adafruit SHT31-D: Sensirion Temperature/Humidity sensors are some of the finest & highest-accuracy devices you can get. And, finally we have some that have a true I2C interface for easy reading. The SHT31-D sensor has an excellent ±2% relative humidity and ±0.3°C accuracy for most uses. We now use the version with a PTFE filter, it'll stay clean while still allowing humidity measurements to work Unlike earlier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
